# Fritzing sketch fritzing (saved by Fritzing 0.9.3b)
breadboards: 1

parts:
  GY-NEO6MV3 = SUP500F [package=sup500f]
  U1 = ESP8266 NodeMCU LoLin base
  Part1 = Adafruit BMP180
  VCC1 = 4 x AAA Battery Mount
  S1 = H-Bridge with L298N
  M1 = DC Motor
  M2 = DC Motor
  Power_plug1 = Power plug

nets:
  GND: GY-NEO6MV3.RX-I, U1.GND1-0, U1.GND1-1, U1.GND3-2, U1.GND8-8, Part1.GND, S1.GND
  N1: GY-NEO6MV3.TX-O, U1.D4-0
  N2: GY-NEO6MV3.GND, U1.D5-0, U1.D5-2
  VCC: GY-NEO6MV3.VCC, U1.3V1-0, U1.3V1-1, U1.3V3-3, Part1.+3V3
  N3: U1.D1-0, Part1.SCL
  N4: U1.D2-0, Part1.SDA
  N5: U1.D3-0, U1.D3-3, S1.IN1
  N6: U1.D6-0, U1.D6-3, S1.IN2
  N7: U1.D7-0, U1.D7-3, S1.IN3
  N8: U1.D8-0, U1.D8-3, S1.IN4
  N9: U1.UI-1, S1.12V
  N10: VCC1.-, Power_plug1.VCC
  N11: VCC1.+, Power_plug1.GND
  N12: S1.M1-01, M2.pin_2
  N13: S1.M1-02, M2.pin_1
  N14: S1.M2-01, M1.pin_2

custom parts:
  ESP8266 NodeMCU LoLin base: ESP8266 based NodeMCU Base
  Adafruit BMP180: This precision sensor from Bosch is the best low-cost sensing solution for measuring barometric pressure and temperature. Because pressure changes with altitude you can also use it as an altimeter! The sensor is soldered onto a PCB with a 3.3V regulator, I2C level shifter and pull-up resistors on the I2C pins. The BMP180 is the next-generation of sensors from Bosch, and replaces the BMP085.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
  H-Bridge with L298N: h-bridge
